# Fritzing sketch Schematics (saved by Fritzing 0.9.3b)
breadboards: 1

parts:
  Part1 = Arduino Uno (Rev3)
  LCD1 = LCD screen
  U2 = MIDI_CONN_FEMALE [package=din_5_female]
  J1 = Piezo Speaker
  R1 = Resistor [tolerance=±5% resistance=220 package="2010 [SMD]"]

nets:
  N1: Part1.D8, LCD1.E
  N2: Part1.D9_PWM, LCD1.RS
  N3: Part1.D10_PWM/SS, LCD1.DB4
  N4: Part1.D11_PWM/MOSI, LCD1.DB7
  N5: Part1.D12/MISO, LCD1.DB6
  N6: Part1.D13/SCK, LCD1.DB5
  N7: Part1.D5_PWM, U2.MIDI_IN
  N8: Part1.D6_PWM, U2.NC1
  N9: Part1.5V, U2.MIDI_OUT, J1.pin2
  N10: Part1.GND, LCD1.LED-, U2.NC3
  N11: J1.pin1, R1.Pin_1
